# Fritzing sketch ESP8266IoTButton (saved by Fritzing 0.9.3b)

parts:
  WeMos_D1_Mini1 = WeMos D1 Mini
  WeMos_D1_Mini_Battery_Shield1 = WeMos D1 Mini Battery Shield
  Part1 = 16 NeoPixel Ring [part_number=1463]
  Part2 = Lithium Ion Polymer Battery 3.7v 150mAh [part_number=1317]  # not connected
  BUTTON1 = Arcade Button (green)

nets:
  3V3: WeMos_D1_Mini1.3V3, WeMos_D1_Mini_Battery_Shield1.3V3
  5V: WeMos_D1_Mini1.5V, WeMos_D1_Mini_Battery_Shield1.5V, Part1.VDD
  N1: WeMos_D1_Mini1.D2, BUTTON1.no_name_yet#1
  N2: WeMos_D1_Mini1.D6, Part1.IN
  N3: WeMos_D1_Mini1.G, WeMos_D1_Mini_Battery_Shield1.G, Part1.GND, BUTTON1.no_name_yet#2

custom parts:
  16 NeoPixel Ring: 16 ultra bright smart LED NeoPixels are arranged in a circle with 1.75" (44.5mm) outer diameter. The rings are 'chainable' - connect the output pin of one to the input pin of another. Use only one microcontroller pin to control as many as you can chain together! Each LED is addressable as the driver chip is inside the LED. Each one has ~18mA constant current drive so the color will be very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
  Lithium Ion Polymer Battery 3.7v 150mAh: Lithium ion polymer (also known as 'lipo' or 'lipoly') batteries are thin, light and powerful. The output ranges from 4.2V when completely charged to 3.7V. This battery has a capacity of 150mAh for a total of about 0.6 Wh. The batteries come pre-attached with a genuine 2-pin JST-PH connector as shown and include the necessary protection circuitry.
  Arcade Button (green): Adafruit Arcade Button (green)
